// Logisim project Design and simulation of an automatic street light control system.circ as structural Verilog: 1 circuit, main circuit main
module main (
  input  Darkness__L,
  input  Motion__M,
  input  Override__O,
  output out_4
);

  wire and_1_out, not_1_out;

  and and_1 (and_1_out, Darkness__L, Motion__M);
  not not_1 (not_1_out, Override__O);
  and and_2 (out_4, and_1_out, not_1_out);

  // Notes on the sheet:
  //   Design and simulation of an automatic street light control system
endmodule
